# Fritzing sketch Arduino-Uno-r3-with-RFID-RC522 (saved by Fritzing 0.9.2b)
breadboards: 1

parts:
  Part2 = RFID-RC522-v2
  Part1 = Arduino Uno (Rev3) - ICSP
  Part3 = MicroSD Card Module
  74HC139N1 = 74HC139N [part_number=74HC139N package="DIP (Dual Inline) [THT]"]
  J1 = Basic Servo
  LCM1602_IIC1 = LCM1602 IIC [part_number="LCM1602 IIC" chip_label="LCM1602 IIC" package="DIP (Dual Inline) [THT]"]
  S1 = Pushbutton [package="[THT]"]
  S2 = Pushbutton [package="[THT]"]
  Power_plug1 = Power plug
  R1 = Resistor [tolerance=±5% resistance=10k package=THT]
  R2 = Resistor [tolerance=±5% resistance=10k package=THT]
  LCD1 = LCD screen

nets:
  N1: Part2.SDA, Part1.D7
  N2: Part2.SCK, Part1.ICSP_SCK, Part3.SCK
  N3: Part2.MOSI, Part1.ICSP_MOSI, Part1.D11_PWM/MOSI, Part3.MOSI
  N4: Part2.MISO, Part1.ICSP_MISO, Part1.D12/MISO, 74HC139N1.1B
  GND: Part2.GND, Part1.GND, Part3.GND, 74HC139N1.GND, J1.gnd, LCM1602_IIC1.GND, S1.Pin_1, S1.Pin_2, S2.Pin_1, S2.Pin_2, Power_plug1.GND
  N5: Part2.RST, Part1.D6_PWM
  N6: Part2.3_3V, Part1.3V3
  N7: Part1.A4/SDA, LCM1602_IIC1.SCL
  N8: Part1.A5/SCL, LCM1602_IIC1.SDA
  N9: Part1.D8, Part3.CS, 74HC139N1.1G_
  N10: Part1.D9_PWM, J1.pulse
  N11: Part1.D2, S1.Pin_3, S1.Pin_4, R1.Pin_1
  N12: Part1.D3_PWM, S2.Pin_3, S2.Pin_4, R2.Pin_1
  VCC: Part1.VIN, Part3.VCC, 74HC139N1.VCC, J1.vcc, LCM1602_IIC1.VCC, Power_plug1.VCC, R1.Pin_0, R2.Pin_0
  N13: Part3.MISO, 74HC139N1.1A
  VSS: LCM1602_IIC1.VSS, LCM1602_IIC1.VDD, LCM1602_IIC1.V0, LCM1602_IIC1.RS, LCM1602_IIC1.RW, LCM1602_IIC1.E, LCM1602_IIC1.D0, LCM1602_IIC1.D1, LCM1602_IIC1.D2, LCM1602_IIC1.D3, LCM1602_IIC1.D4, LCM1602_IIC1.D5, LCM1602_IIC1.D6, LCM1602_IIC1.D7, LCM1602_IIC1.A, LCM1602_IIC1.K, LCD1.VSS, LCD1.VDD, LCD1.V0, LCD1.RS, LCD1.R/W, LCD1.E, LCD1.DB0, LCD1.DB1, LCD1.DB2, LCD1.DB3, LCD1.DB4, LCD1.DB5, LCD1.DB6, LCD1.DB7, LCD1.LED+, LCD1.LED-

custom parts:
  RFID-RC522-v2: A simple China made RFID-RC522 Reader; do check the pin labels, as this is a MFRC522 based clone.
  LCM1602 IIC: I2C-Module to use a 1602 or 2004 LCD on with the wire.h libory Serial LCD Modul
